// Logisim project DSD_LAB_7_1.circ as structural Verilog: 1 circuit, main circuit main
module main (
  input  [3:0] A,
  input  C0,
  input  [3:0] B,
  output S0,
  output C1,
  output [3:0] out_6,
  output S1,
  output C2,
  output S2,
  output C3,
  output S3,
  output C4
);

  wire and_1_out, and_2_out, and_3_out, G0_out, G1_out, G2_out, G3_out, or_1_out, or_3_out, or_4_out, P0_out,
       P1_out, P2_out, P3_out, P3C3_out;

  xor P0 (P0_out, A[0], B[0]);
  and G0 (G0_out, A[0], B[0]);
  xor P1 (P1_out, A[1], B[1]);
  and G1 (G1_out, A[1], B[1]);
  xor P2 (P2_out, A[2], B[2]);
  and G2 (G2_out, A[2], B[2]);
  xor P3 (P3_out, A[3], B[3]);
  and G3 (G3_out, A[3], B[3]);
  xor xor_1 (out_6[0], P0_out, C0);
  and and_1 (and_1_out, P0_out, C0);
  or or_1 (or_1_out, and_1_out, G0_out);
  xor xor_2 (out_6[1], P1_out, or_1_out);
  and and_2 (and_2_out, P1_out, or_1_out);
  xor xor_3 (out_6[2], P2_out, or_3_out);
  and and_3 (and_3_out, P2_out, or_3_out);
  or or_2 (C1, and_1_out, G0_out);
  or or_3 (or_3_out, G1_out, and_2_out);
  or or_4 (or_4_out, and_3_out, G2_out);
  xor xor_4 (out_6[3], P3_out, or_4_out);
  and P3C3 (P3C3_out, P3_out, or_4_out);
  or or_5 (C2, and_2_out, G1_out);
  or or_6 (C3, and_3_out, G2_out);
  or or_7 (C4, P3C3_out, G3_out);

  assign S0 = out_6[0];
  assign S1 = out_6[1];
  assign S2 = out_6[2];
  assign S3 = out_6[3];
endmodule
